// Logisim project SR.circ as structural Verilog: 1 circuit, main circuit main
module main (
);

  wire multiplexer_1_out;

  Multiplexer #(.enable("false")) multiplexer_1 (.out(multiplexer_1_out));  // open: in0, in1, sel
  D_Flip_Flop d_ff_1 (.D(multiplexer_1_out));  // open: clk, Q, Qn, preset, en, reset
  D_Flip_Flop d_ff_2 ();  // open: clk, D, Q, Qn, preset, en, reset
  Multiplexer #(.enable("false")) multiplexer_2 ();  // open: in0, in1, out, sel
  Multiplexer #(.enable("false")) multiplexer_3 ();  // open: in0, in1, out, sel
  D_Flip_Flop d_ff_3 ();  // open: clk, D, Q, Qn, preset, en, reset
  Multiplexer #(.enable("false")) multiplexer_4 ();  // open: in0, in1, out, sel
  D_Flip_Flop d_ff_4 ();  // open: clk, D, Q, Qn, preset, en, reset
  Multiplexer #(.enable("false")) multiplexer_5 ();  // open: in0, in1, out, sel
  D_Flip_Flop d_ff_5 ();  // open: clk, D, Q, Qn, preset, en, reset
  Multiplexer #(.enable("false")) multiplexer_6 ();  // open: in0, in1, out, sel
  D_Flip_Flop d_ff_6 ();  // open: clk, D, Q, Qn, preset, en, reset
  D_Flip_Flop d_ff_7 ();  // open: clk, D, Q, Qn, preset, en, reset
  Multiplexer #(.enable("false")) multiplexer_7 ();  // open: in0, in1, out, sel
  Multiplexer #(.enable("false")) multiplexer_8 ();  // open: in0, in1, out, sel
endmodule
